# Fritzing sketch Schema Collegamenti andreino (saved by Fritzing 0.9.3b)
breadboards: 1

parts:
  S1 = H-Bridge with L298N
  VCC1 = 4 x AAA Battery Mount
  M1 = DC Motor
  M2 = DC Motor
  Componente1 = Arduino Uno (Rev3) - ICSP
  VCC2 = 4 x AAA Battery Mount
  M3 = DC Motor
  M4 = DC Motor
  hc-sr1 = hc-sr04
  S2 = Pololu QTR-8 Reflectabce Sensor array [package=THT]
  JACK1 = 2.1mm Barrel Jack with Terminal Block
  VCC3 = Battery block 9V
  hc-sr2 = hc-sr04

nets:
  N1: S1.12V, VCC1.+
  GND: S1.GND, Componente1.GND, VCC2.-, hc-sr1.GND, S2.pin1, S2.pin15, hc-sr2.GND
  5V: S1.5V, Componente1.5V
  N2: S1.ENA, Componente1.D9_PWM
  N3: S1.IN1, Componente1.D2
  N4: S1.IN2, Componente1.D4
  N5: S1.IN3, Componente1.D8
  N6: S1.IN4, Componente1.D7
  N7: S1.ENB, Componente1.D3_PWM
  N8: S1.M1-01, M1.pin_2, M3.pin_1
  N9: S1.M1-02, M1.pin_1, M3.pin_2
  N10: S1.M2-01, M2.pin_2, M4.pin_1
  N11: S1.M2-02, M2.pin_1, M4.pin_2
  N12: Componente1.A0, S2.pin12
  N13: Componente1.A1, S2.pin11
  N14: Componente1.A2, S2.pin10
  N15: Componente1.A3, S2.pin9
  N16: Componente1.A4/SDA, S2.pin8
  N17: Componente1.A5/SCL, S2.pin7
  N18: Componente1.D10_PWM/SS, hc-sr2.Echo
  N19: Componente1.D11_PWM/MOSI, hc-sr2.Trig
  N20: Componente1.D5_PWM, hc-sr1.Echo
  N21: Componente1.D6_PWM, hc-sr1.Trig
  VCC: Componente1.VIN, hc-sr1.VCC, S2.pin2, S2.pin14, hc-sr2.VCC
  N22: JACK1.POS, VCC3.+
  N23: JACK1.NEG, VCC3.-

notes:
  Collegamento in serie

custom parts:
  H-Bridge with L298N: h-bridge
