# Fritzing sketch Schema elettrico andreino (saved by Fritzing 0.9.3b)

parts:
  S1 = H-Bridge with L298N
  Arduino_Uno = Arduino Uno (Rev3) - ICSP
  Slot1_Batterie_4x = 4 x AAA Battery Mount
  Slot2_Batterie_4x = 4 x AAA Battery Mount
  S3 = Pololu QTR-8 Reflectabce Sensor array [package=THT]
  M6 = DC Motor
  M7 = DC Motor
  M8 = DC Motor
  M9 = DC Motor
  hc-sr1 = hc-sr04
  JACK1 = 2.1mm Barrel Jack with Terminal Block
  Batteria = Battery block 9V
  hc-sr2 = hc-sr04

nets:
  N1: S1.12V, Slot1_Batterie_4x.+
  GND: S1.GND, Arduino_Uno.GND, Arduino_Uno.D8, Arduino_Uno.D4, Arduino_Uno.D7, Arduino_Uno.VIN, Slot2_Batterie_4x.-, S3.pin1, S3.pin14, S3.pin15, S3.pin22, hc-sr1.Trig, hc-sr2.Trig
  5V: S1.5V, Arduino_Uno.5V
  N2: S1.ENA, Arduino_Uno.ICSP_MOSI, Arduino_Uno.D11_PWM/MOSI
  N3: S1.IN1, Arduino_Uno.D9_PWM
  N4: S1.IN2, Arduino_Uno.D5_PWM
  N5: S1.IN3, Arduino_Uno.D10_PWM/SS
  N6: S1.IN4, Arduino_Uno.D6_PWM
  N7: S1.ENB, Arduino_Uno.D3_PWM
  N8: S1.M1-01, M8.pin_2, M9.pin_1
  N9: S1.M1-02, M8.pin_1, M9.pin_2
  N10: S1.M2-01, M6.pin_2, M7.pin_1
  N11: S1.M2-02, M6.pin_1, M7.pin_2
  N12: Arduino_Uno.A0, S3.pin12
  N13: Arduino_Uno.A1, S3.pin11
  N14: Arduino_Uno.A2, S3.pin10
  N15: Arduino_Uno.A3, S3.pin9
  N16: Arduino_Uno.A4/SDA, S3.pin8
  N17: Arduino_Uno.A5/SCL, S3.pin7
  N18: Arduino_Uno.D2, hc-sr1.Echo
  N19: JACK1.POS, Batteria.+
  N20: JACK1.NEG, Batteria.-

notes:
  Collegamento in serie
  Motori di destra
  Motori di sinistra
  è collecato all'arduino
  (è un'adattatore)

custom parts:
  H-Bridge with L298N: h-bridge
